# Fritzing sketch 두더지게임 (saved by Fritzing 0.9.3b)
breadboards: 1

parts:
  부품1 = Arduino Uno (Rev3)
  S1 = Pushbutton [package="[THT]"]
  S2 = Pushbutton [package="[THT]"]
  LED1 = LED - 5mm [color="Red (633nm)" package="5 mm [THT]"]
  LED2 = LED - 5mm [color="Red (633nm)" package="5 mm [THT]"]
  LED3 = LED - 5mm [color="Red (633nm)" package="5 mm [THT]"]
  J1 = Piezo Speaker
  R1 = Resistor [tolerance=±5% resistance=220 package=THT]
  LED4 = LED - 5mm [color="Green (565nm)" package="5 mm [THT]"]
  R2 = Resistor [tolerance=±5% resistance=220 package=THT]
  R3 = Resistor [tolerance=±5% resistance=220 package=THT]
  R4 = Resistor [tolerance=±5% resistance=220 package=THT]
  R5 = Resistor [tolerance=±5% resistance=220 package=THT]
  S3 = Pushbutton [package="[THT]"]
  LED5 = LED - 5mm [color="Green (565nm)" package="5 mm [THT]"]
  S4 = Pushbutton [package="[THT]"]
  LED6 = LED - 5mm [color="Green (565nm)" package="5 mm [THT]"]
  S5 = Pushbutton [package="[THT]"]
  LED7 = LED - 5mm [color="Green (565nm)" package="5 mm [THT]"]
  S6 = Pushbutton [package="[THT]"]
  LED8 = LED - 5mm [color="Green (565nm)" package="5 mm [THT]"]
  R6 = Resistor [tolerance=±5% resistance=220 package=THT]

nets:
  N1: 부품1.A0, S2.Pin_1, S2.Pin_2
  N2: 부품1.A1, S3.Pin_1, S3.Pin_2
  N3: 부품1.A2, S4.Pin_1, S4.Pin_2
  N4: 부품1.A3, S5.Pin_1, S5.Pin_2
  N5: 부품1.A4/SDA, S6.Pin_1, S6.Pin_2
  N6: 부품1.D8, J1.pin2
  N7: 부품1.D10_PWM/SS, LED1.anode
  N8: 부품1.D11_PWM/MOSI, LED2.anode
  N9: 부품1.D12/MISO, LED3.anode
  N10: 부품1.D0/RX, 부품1.GND, S1.Pin_3, S1.Pin_4, S2.Pin_3, S2.Pin_4, J1.pin1, R1.Pin_1, LED4.cathode, S3.Pin_3, S3.Pin_4, LED5.cathode, S4.Pin_3, S4.Pin_4, LED6.cathode, S5.Pin_3, S5.Pin_4, LED7.cathode, S6.Pin_3, S6.Pin_4, LED8.cathode
  N11: 부품1.D1/TX, R2.Pin_1
  N12: 부품1.D2, R3.Pin_1
  N13: 부품1.D3_PWM, R4.Pin_1
  N14: 부품1.D4, R5.Pin_1
  N15: 부품1.D5_PWM, R6.Pin_1
  N16: 부품1.5V, S1.Pin_1, S1.Pin_2
  N17: LED1.cathode, LED2.cathode, LED3.cathode, R1.Pin_0
  N18: LED4.anode, R2.Pin_0
  N19: R3.Pin_0, LED5.anode
  N20: R4.Pin_0, LED6.anode
  N21: R5.Pin_0, LED7.anode
  N22: LED8.anode, R6.Pin_0
